// Logisim project teste.circ as structural Verilog: 1 circuit, main circuit main
module main (
  input  [2:0] in_1,
  input  [2:0] in_2,
  output [2:0] out_3
);

  assign out_3 = in_1 & in_2;  // AND_Gate and_1, 3 bits wide
endmodule
