// Logisim project Ketllyn.a-PortasOR-AND.circ as structural Verilog: 2 circuits, main circuit PortaAND-bits
module PortaAND_bits (
  input  [3:0] in_1,
  input  [3:0] in_2,
  output [3:0] out_3
);

  Hex_Digit_Display hex_digit_display_1 (.value(in_2));  // open: dp
  Hex_Digit_Display hex_digit_display_2 (.value(in_1));  // open: dp
  assign out_3 = in_1 & in_2;  // AND_Gate and_1, 4 bits wide
  Hex_Digit_Display hex_digit_display_3 (.value(out_3));  // open: dp
endmodule

module PortaOR_4bits (
  input  [3:0] in_1,
  input  [3:0] in_2,
  output [3:0] out_3
);

  wire [3:0] or_1_out;

  Hex_Digit_Display hex_digit_display_1 (.value(in_2));  // open: dp
  Hex_Digit_Display hex_digit_display_2 (.value(in_1));  // open: dp
  assign or_1_out = in_1 | in_2;  // OR_Gate or_1, 4 bits wide
  Hex_Digit_Display hex_digit_display_3 (.value(out_3));  // open: dp
endmodule
