// Logisim project PROCESSADOR KET COMPLETO.circ as structural Verilog: 5 circuits, main circuit Banco de Registradores
module Banco_de_Registradores (
  input  [2:0] Real_Register_1,
  input  [2:0] Real_registrer_2,
  input  [7:0] Write_Data,
  input  Reg_Write,
  input  [2:0] Write_Registrer,
  input  CLOCK,
  input  CLEAR,
  output [7:0] Read_Data_1,
  output [7:0] Read_Data_2
);

  wire WE0, WE1, WE2, WE3, WE4, WE5, WE6, WE7;
  wire [7:0] demultiplexer_2_out0, demultiplexer_2_out1, demultiplexer_2_out2, demultiplexer_2_out3,
       demultiplexer_2_out4, demultiplexer_2_out5, demultiplexer_2_out7, Reg_0, Reg_1, Reg_2, Reg_3, Reg_4,
       Reg_5;

  Demultiplexer #(.select(3), .enable("false")) demultiplexer_1 (
    .out0(WE0), .out1(WE1), .out2(WE2), .out3(WE3), .out4(WE4), .out5(WE5), .out6(WE6), .out7(WE7),
    .in(Reg_Write), .sel(Write_Registrer));
  Demultiplexer #(.select(3), .width(8), .enable("false")) demultiplexer_2 (
    .out0(demultiplexer_2_out0), .out1(demultiplexer_2_out1), .out2(demultiplexer_2_out2),
    .out3(demultiplexer_2_out3), .out4(demultiplexer_2_out4), .out5(demultiplexer_2_out5),
    .out6(demultiplexer_2_out5), .out7(demultiplexer_2_out7), .in(Write_Data), .sel(Write_Registrer));
  Register Reg_7 (.D(demultiplexer_2_out7), .en(WE7), .Q(Reg_5), .clk(CLOCK), .clr(CLEAR));
  Register u_Reg_0 (.D(demultiplexer_2_out0), .en(WE0), .Q(Reg_0), .clk(CLOCK), .clr(CLEAR));
  Register u_Reg_1 (.D(demultiplexer_2_out1), .en(WE1), .Q(Reg_1), .clk(CLOCK), .clr(CLEAR));
  Register Reg2 (.D(demultiplexer_2_out2), .en(WE2), .Q(Reg_2), .clk(CLOCK), .clr(CLEAR));
  Register u_Reg_3 (.D(demultiplexer_2_out3), .en(WE3), .Q(Reg_3), .clk(CLOCK), .clr(CLEAR));
  Register u_Reg_4 (.D(demultiplexer_2_out4), .en(WE4), .Q(Reg_4), .clk(CLOCK), .clr(CLEAR));
  Register u_Reg_5 (.D(demultiplexer_2_out5), .en(WE5), .Q(Reg_5), .clk(CLOCK), .clr(CLEAR));
  Register Reg_6 (.D(demultiplexer_2_out5), .Q(Reg_5), .clk(CLOCK), .clr(CLEAR));  // open: en
  Multiplexer #(.select(3), .width(8)) multiplexer_1 (
    .in0(Reg_0), .in1(Reg_1), .in2(Reg_2), .in3(Reg_3), .in4(Reg_4), .in5(Reg_5), .in6(Reg_5), .in7(Reg_5),
    .out(Read_Data_1), .sel(Real_Register_1));  // open: en
  Multiplexer #(.select(3), .width(8)) multiplexer_2 (
    .in0(Reg_0), .in1(Reg_1), .in2(Reg_2), .in3(Reg_3), .in4(Reg_4), .in5(Reg_5), .in6(Reg_5), .in7(Reg_5),
    .out(Read_Data_2), .sel(Real_registrer_2));  // open: en

  // Other names for the same wires on the sheet: Real_Register2[2:0] = Real_registrer_2;
  //   Real_Registrer_1[2:0] = Real_Register_1; Reg_6[7:0] = Reg_5; Reg_7[7:0] = Reg_5
endmodule

// rs
module \PC_e_Memória_de_instruções  (
  input  in_1
);

  wire ALUSrc, and_1_out, Branch, clock_1_out, Jump, MemRead, MemToReg, MemWrite, not_1_out, RedDst,
       RedWrite, tunnel, \unidade_lógica_aritmética_ula_1_igual ;
  wire [1:0] ALUOp;
  wire [2:0] controle_ula_1_ulactrl, multiplexer_2_out, opcode, rs, rt;
  wire [2:2] rd;
  wire [7:0] adder_1_out, addres_lmm, banco_de_registradores_1_p3, banco_de_registradores_1_p6, contRT,
       multiplexer_1_out, multiplexer_3_out, ram_1_data, register_1_q,
       \unidade_lógica_aritmética_ula_1_resultado ;

  Clock clock_1 (.out(clock_1_out));
  Register register_1 (.D(multiplexer_1_out), .Q(register_1_q), .clk(clock_1_out), .clr(in_1));  // open: en
  Adder adder_1 (.a(8'h1), .b(register_1_q), .out(adder_1_out));  // open: cin, cout
  ROM #(.dataWidth(18)) rom_1 (.addr(register_1_q), .data({opcode, rs, rt, rd[2], addres_lmm}));  // open: sel
  Multiplexer #(.width(8), .enable("false")) multiplexer_1 (
    .in0(adder_1_out), .in1(addres_lmm), .out(multiplexer_1_out), .sel(tunnel));
  Unidade_de_Controle unidade_de_controle_1 (
    .OPCODE(opcode), .RegDst(RedDst), .RegWrite(RedWrite), .ALUSrc(ALUSrc), .MemWrite(MemWrite),
    .MemRead(MemRead), .MemToReg(MemToReg), .Branch(Branch), .Jump(Jump), .ALUOP(ALUOp));
  Multiplexer #(.width(3), .enable("false")) multiplexer_2 (
    .in0(rt), .in1({rd[2], addres_lmm[7:6]}), .out(multiplexer_2_out), .sel(RedDst));
  not not_1 (not_1_out, clock_1_out);
  // Banco_de_Registradores banco_de_registradores_1: pin names not known; wires that end beside it: rs, rt, banco_de_registradores_1_p3, RedWrite, multiplexer_2_out, banco_de_registradores_1_p6, contRT
  Multiplexer #(.width(8)) multiplexer_3 (
    .in0(contRT), .in1(addres_lmm), .out(multiplexer_3_out), .sel(ALUSrc));  // open: en
  Controle_ULA controle_ula_1 (.Funct(addres_lmm[2:0]), .ULAOp(ALUOp), .ULACtrl(controle_ula_1_ulactrl));
  \Unidade_Lógica_Aritmética___ULA  \unidade_lógica_aritmética_ula_1  (
    .Entrada_1(banco_de_registradores_1_p6), .Entrada_2(multiplexer_3_out),
    .\FUNÇÃO (controle_ula_1_ulactrl), .Shamt(addres_lmm[5:3]),
    .RESULTADO(\unidade_lógica_aritmética_ula_1_resultado ), .Igual(\unidade_lógica_aritmética_ula_1_igual ));
  and and_1 (and_1_out, Branch, \unidade_lógica_aritmética_ula_1_igual );
  RAM #(.bus("separate")) ram_1 (
    .addr(\unidade_lógica_aritmética_ula_1_resultado ), .din(contRT), .data(ram_1_data), .str(MemWrite),
    .clk(not_1_out), .ld(MemRead), .clr(in_1));  // open: sel
  or or_1 (tunnel, Jump, and_1_out);
  Multiplexer #(.width(8), .enable("false")) multiplexer_4 (
    .in0(ram_1_data), .in1(\unidade_lógica_aritmética_ula_1_resultado ), .out(banco_de_registradores_1_p3),
    .sel(MemToReg));

  // Other names for the same wires on the sheet: funct[2:0] = addres_lmm[2:0]; rd[1:0] = addres_lmm[7:6];
  //   shamt[2:0] = addres_lmm[5:3]

  // Notes on the sheet:
  //   contents of rom_1 (hex, n*v repeats v):
  //   0 3ffff 2 6 14*0 1
endmodule

module \Unidade_Lógica_Aritmética___ULA  (
  input  [7:0] Entrada_1,
  input  [7:0] Entrada_2,
  input  [2:0] \FUNÇÃO ,
  input  [2:0] Shamt,
  output [7:0] RESULTADO,
  output Igual
);

  wire comparator_1_lt;
  wire [7:0] adder_1_out, bit_extender_1_out, COMP1, COMP2, DESDir, DESDir2, DESEsq, DESEsq2, DIV1, DIV2,
       DIVi1, divider_1_out, MULTI1, MULTI2, multiplier_1_out, NEG, negator_1_out, shifter_1_out,
       shifter_2_out, SOMA1, SOMA2, SUB1, SUB2, subtractor_1_out;

  Demultiplexer #(.select(3), .width(8), .enable("false")) demultiplexer_1 (
    .out0(NEG), .out1(SOMA2), .out2(SUB2), .out3(MULTI2), .out4(DIV2), .out5(COMP2), .out6(DESEsq2),
    .out7(DESDir2), .in(Entrada_1), .sel(\FUNÇÃO ));
  Demultiplexer #(.select(3), .width(8), .enable("false")) demultiplexer_2 (
    .out1(SOMA1), .out2(SUB1), .out3(MULTI1), .out4(DIVi1), .out5(COMP1), .in(Entrada_2), .sel(\FUNÇÃO ));  // open: out0, out6, out7
  Negator negator_1 (.in(NEG), .out(negator_1_out));
  Adder adder_1 (.a(SOMA2), .b(SOMA1), .out(adder_1_out));  // open: cin, cout
  Subtractor subtractor_1 (.a(SUB2), .b(SUB1), .out(subtractor_1_out));  // open: bin, bout
  Multiplier multiplier_1 (.a(MULTI2), .b(MULTI1), .out(multiplier_1_out));  // open: cin, cout
  Divider divider_1 (.a(DIV2), .b(DIV1), .out(divider_1_out));  // open: upper, rem
  Comparator comparator_1 (.a(COMP2), .b(COMP1), .eq(Igual), .lt(comparator_1_lt));  // open: gt
  Shifter shifter_1 (.in(DESEsq), .\dist (Shamt), .out(shifter_1_out));
  Shifter #(.shift("lr")) shifter_2 (.in(DESDir), .\dist (Shamt), .out(shifter_2_out));
  assign bit_extender_1_out = {{7{1'b0}}, comparator_1_lt};  // Bit_Extender bit_extender_1
  Multiplexer #(.select(3), .width(8), .enable("false")) multiplexer_1 (
    .in0(negator_1_out), .in1(adder_1_out), .in2(subtractor_1_out), .in3(multiplier_1_out),
    .in4(divider_1_out), .in5(bit_extender_1_out), .in6(shifter_1_out), .in7(shifter_2_out), .out(RESULTADO),
    .sel(\FUNÇÃO ));
endmodule

module Controle_ULA (
  input  [2:0] Funct,
  input  [1:0] ULAOp,
  output [2:0] ULACtrl
);

  Multiplexer #(.select(2), .width(3)) multiplexer_1 (
    .in0(3'b000), .in1(3'b101), .in2(Funct), .in3(3'b000), .out(ULACtrl), .sel(ULAOp));  // open: en
endmodule

module Unidade_de_Controle (
  input  [2:0] OPCODE,
  output RegDst,
  output RegWrite,
  output ALUSrc,
  output MemWrite,
  output MemRead,
  output MemToReg,
  output Branch,
  output Jump,
  output [1:0] ALUOP
);

  wire and_1_out, and_4_out, and_5_out, and_8_out, and_9_out, nor_2_out;

  nor nor_1 (RegDst, OPCODE[0], OPCODE[1], OPCODE[2]);
  nor nor_2 (nor_2_out, OPCODE[1], OPCODE[2]);
  and and_1 (and_1_out, ~OPCODE[0], ~OPCODE[1], OPCODE[2]);  // AND_Gate
  ExactlyOne xor_1 (.out(ALUSrc), .in0(OPCODE[0]), .in1(OPCODE[1]), .in2(OPCODE[2]));
  and and_2 (MemWrite, ~OPCODE[0], OPCODE[1], ~OPCODE[2]);  // AND_Gate
  and and_3 (MemRead, OPCODE[0], ~OPCODE[1], ~OPCODE[2]);  // AND_Gate
  and and_4 (and_4_out, ~OPCODE[0], ~OPCODE[1], ~OPCODE[2]);  // AND_Gate
  and and_5 (and_5_out, ~OPCODE[0], ~OPCODE[1], OPCODE[2]);  // AND_Gate
  and and_6 (Branch, OPCODE[0], OPCODE[1], ~OPCODE[2]);  // AND_Gate
  and and_7 (Jump, OPCODE[0], OPCODE[1], OPCODE[2]);
  and and_8 (and_8_out, OPCODE[0], OPCODE[1], ~OPCODE[2]);  // AND_Gate
  and and_9 (and_9_out, ~OPCODE[0], ~OPCODE[1], OPCODE[2]);  // AND_Gate
  and and_10 (ALUOP[1], ~OPCODE[0], OPCODE[1], ~OPCODE[2]);  // AND_Gate
  or or_1 (RegWrite, nor_2_out, and_1_out);
  or or_2 (MemToReg, and_4_out, and_5_out);
  or or_3 (ALUOP[1], and_8_out, and_9_out);

  assign ALUOP[0] = ALUOP[1];
endmodule
